# Fritzing sketch ble-fan (saved by Fritzing 0.9.2b)
circuit board: 2.95cm x 1.95cm
breadboards: 1

parts:
  BAT = SO08 [chip_label=IC package=SO08]
  Debug = female pin header, 5 pins [form="♀ (female)"]
  CC2542 = CC2541-small [part_number=cc2540]
  10uF2 = Tantalum Capacitor [capacitance="1 μF" package="A 3216 [SMD, tantalum]"]
  C4 = Tantalum Capacitor [capacitance=47µF package="A 3216 [SMD, tantalum]"]
  C3 = Tantalum Capacitor [capacitance=10µF package="A 3216 [SMD, tantalum]"]
  10uF1 = Tantalum Capacitor [capacitance="1 μF" package="A 3216 [SMD, tantalum]"]
  U3 = LM3480IM4 [package=sot23-3]
  Q1 = NPN-Transistor [package="TO92 [THT]"]
  R1 = Resistor [tolerance=±5% resistance=220 package=THT]
  M1 = DC Motor

nets:
  5V: BAT.V+, C4.+, C3.+, 10uF1.+, U3.IN, M1.pin_1
  GND: BAT.V-, Debug.pin1, CC2542.GND, 10uF2.-, C4.-, C3.-, 10uF1.-, U3.GND, Q1.E
  3.3V: Debug.pin2, CC2542.3.3V, 10uF2.+, U3.OUT
  N1: Debug.pin3, CC2542.P2.1
  N2: Debug.pin4, CC2542.P2.2
  N3: Debug.pin5, CC2542.RESET
  N4: CC2542.P2.0, R1.Pin_0
  N5: Q1.B, R1.Pin_1
  N6: Q1.C, M1.pin_2

notes:
  B-
  B+
  Power
  MCU

// code stored in the sketch: Untitled2.ino
LDO - use small one..
