# Fritzing sketch ble-pc (saved by Fritzing 0.9.1b)
circuit board: 2.63762cm x 3.05025cm
breadboards: 1

parts:
  PWR = Optocoupler [package=THT]
  RESET = Optocoupler [package=THT]
  HDD_LED = Optocoupler [package=THT]
  PWR_LED = Optocoupler [package=THT]
  HDD = female pin header, 2 pins [form="♀ (female)"]
  PWR_2 = female pin header, 2 pins [form="♀ (female)"]
  CC2541 = CC2541 [chip_label=IC package="DIP (Dual Inline) [THT]"]
  VCC1 = Battery
  J1 = female pin header, 4 pins [form="♀ (female)"]
  R6 = Resistor [tolerance=±5% resistance=10k package="0603 [SMD]"]
  R1 = Resistor [tolerance=±5% resistance=470 package="0603 [SMD]"]
  R2 = Resistor [tolerance=±5% resistance=470 package="0603 [SMD]"]
  R10 = Resistor [tolerance=±5% resistance=10k package="0603 [SMD]"]
  R4 = Resistor [tolerance=±5% resistance=470 package="0603 [SMD]"]
  R3 = Resistor [tolerance=±5% resistance=470 package="0603 [SMD]"]
  J2 = double row female pin header, 2 pins [form="♀ (female)"]
  DS18B20 = DS18B20 [package="TO92 [THT]"]
  R11 = Resistor [tolerance=±5% resistance=4.7k package="0603 [SMD]"]
  part = Resistor [tolerance=±5% resistance=220 package="0603 [SMD]"]  # not connected

nets:
  N1: PWR.Pin_1, R1.Pin_1
  GND: PWR.Pin_2, RESET.Pin_2, HDD_LED.Pin_4, PWR_LED.Pin_4, CC2541.GND, VCC1.-, DS18B20.GND
  N2: PWR.Pin_4, J1.pin1, J1.pin4
  N3: PWR.Pin_5, J1.pin2, J1.pin3
  N4: RESET.Pin_1, R2.Pin_0
  N5: RESET.Pin_4, J2.pin1
  N6: RESET.Pin_5, J2.pin2
  N7: HDD_LED.Pin_1, R3.Pin_0
  N8: HDD_LED.Pin_2, HDD.pin2
  N9: HDD_LED.Pin_5, CC2541.P1.2, R6.Pin_1
  N10: PWR_LED.Pin_1, R4.Pin_0
  N11: PWR_LED.Pin_2, PWR_2.pin2
  N12: PWR_LED.Pin_5, CC2541.P1.3, R10.Pin_0
  N13: HDD.pin1, R3.Pin_1
  N14: PWR_2.pin1, R4.Pin_1
  N15: CC2541.P1.1, DS18B20.DQ, R11.Pin_0
  N16: CC2541.P1.0, DS18B20.VDD, R11.Pin_1
  N17: CC2541.VDD, VCC1.+, R6.Pin_0, R10.Pin_1
  N18: CC2541.P0.1, R2.Pin_1
  N19: CC2541.P0.0, R1.Pin_0

custom parts:
  CC2541: A DIP stand-in part for whatever IC you want. With 26 pins on a 300mil dual inline package (DIP) footprint.
  DS18B20: A standard NPN-transistor
