# Fritzing sketch ts2_ir_remote2-lite (saved by Fritzing 0.8.3b)
circuit board: 3.26311cm x 2.40981cm
breadboards: 1

parts:
  IR_LED = LED - 5mm [color="Infrared (850nm)" package="5 mm [THT]"]
  IR_TR = NPN-Transistor [package="TO92 [THT]"]
  IR_R = Resistor [tolerance=±5% resistance=4.7k package=THT]
  CC2540 = CC2540 [part_number=cc2540]
  VCC2 = CR2032

nets:
  N1: IR_LED.cathode, IR_TR.C
  N2: IR_LED.anode, CC2540.3.3V, VCC2.+
  GND: IR_TR.E, CC2540.GND, VCC2.-
  N3: IR_TR.B, IR_R.Pin_1
  N4: IR_R.Pin_0, CC2540.P1.1

notes:
  +
  -

custom parts:
  CR2032: Your standard 2x AA battery pack (3 Volts)
