# Fritzing sketch ts2_ir_remote2 (saved by Fritzing 0.8.3b)
circuit board: 3.26311cm x 2.40981cm
breadboards: 1

parts:
  IR_LED = LED - 5mm [color="Infrared (850nm)" package="5 mm [THT]"]
  IR_TR = NPN-Transistor [package="TO92 [THT]"]
  IR_R = Resistor [tolerance=±5% resistance=4.7k package=THT]
  R3_-_optional = Resistor [tolerance=±5% resistance=10k package=THT]
  LIGHT_-_optional = Photocell (LDR) [package=THT]
  CC2540 = CC2540 [part_number=cc2540]
  R9_-_optional = Resistor [tolerance=±5% resistance=4.7k package=THT]
  DS18B20_-_optional = DS18B20 [chip_label=? package=THT]
  VCC2 = CR2032

nets:
  N1: IR_LED.cathode, IR_TR.C
  3.3V: IR_LED.anode, CC2540.3.3V, R9_-_optional.Pin_0, DS18B20_-_optional.VDD, VCC2.+
  GND: IR_TR.E, LIGHT_-_optional.pin_1, CC2540.GND, DS18B20_-_optional.GND, VCC2.-
  N2: IR_TR.B, IR_R.Pin_1
  N3: IR_R.Pin_0, CC2540.P1.1
  N4: R3_-_optional.Pin_0, CC2540.P1.4
  N5: R3_-_optional.Pin_1, LIGHT_-_optional.pin_0, CC2540.P0.0
  N6: CC2540.P2.0, R9_-_optional.Pin_1, DS18B20_-_optional.DQ

notes:
  +
  -

custom parts:
  DS18B20: A dummy, proxy, ersatz, stand-in part for whatever you want. With 3 pins on a 100 mil inline pin header footprint.
  CR2032: Your standard 2x AA battery pack (3 Volts)
